# Fritzing sketch FYPSchematic (saved by Fritzing 0.9.10b)

parts:
  S1 = H-Bridge with L298N
  VCC1 = 4 x AAA Battery Mount
  M1 = DC Motor [voltage_(max)=6V voltage_(min)=3V]
  M2 = DC Motor [voltage_(max)=6V voltage_(min)=3V]
  Raspberry_Pi1 = Raspberry Pi 4B

nets (from the breadboard view):
  N1: S1.12V, VCC1.+
  GND: S1.GND, VCC1.-, Raspberry_Pi1.GND
  5V: S1.5V, Raspberry_Pi1.5V
  N2: S1.ENA, Raspberry_Pi1.GPIO14
  N3: S1.IN1, Raspberry_Pi1.GPIO15
  N4: S1.IN2, Raspberry_Pi1.GPIO18
  N5: S1.IN3, Raspberry_Pi1.GPIO8
  N6: S1.IN4, Raspberry_Pi1.GPIO7
  N7: S1.ENB, Raspberry_Pi1.GPIO25
  N8: S1.M1-01, M1.pin_2
  N9: S1.M1-02, M1.pin_1
  N10: S1.M2-01, M2.pin_2
  N11: S1.M2-02, M2.pin_1

custom parts:
  H-Bridge with L298N: h-bridge
